// Logisim project Classlib.circ as structural Verilog: 11 circuits, main circuit HA_1
module HA_1 (
  input  A,
  input  B,
  output COUT__AB,
  output SUM__AB_prime__A_prime_B
);

  wire A_prime_B_out, AB_prime_out, not_1_out, not_2_out;

  not not_1 (not_1_out, B);
  not not_2 (not_2_out, A);
  and AB_prime (AB_prime_out, A, not_1_out);
  and A_prime_B (A_prime_B_out, not_2_out, B);
  and AB (COUT__AB, B, A);
  or or_1 (SUM__AB_prime__A_prime_B, AB_prime_out, A_prime_B_out);
endmodule

module FA_1 (
  input  A,
  input  Cin,
  input  B,
  output SUM,
  output Cout
);

  wire AB_out, XAB_out, XABC_out;

  and AB (AB_out, B, A);
  xor XAB (XAB_out, A, B);
  xor XABXC (SUM, Cin, XAB_out);
  and XABC (XABC_out, Cin, XAB_out);
  or or_1 (Cout, XABC_out, AB_out);
endmodule

// A
module FA_4 (
  input  A0,
  input  A1,
  input  A2,
  input  A3,
  input  B0,
  input  B1,
  input  B2,
  input  B3,
  input  CIN,
  output S0,
  output S1,
  output S2,
  output S3,
  output COUT
);

  wire fa_1_1_cout, fa_1_2_cout, fa_1_3_cout;

  FA_1 fa_1_1 (.A(A0), .Cin(CIN), .B(B0), .SUM(S0), .Cout(fa_1_1_cout));
  FA_1 fa_1_2 (.A(A1), .Cin(fa_1_1_cout), .B(B1), .SUM(S1), .Cout(fa_1_2_cout));
  FA_1 fa_1_3 (.A(A2), .Cin(fa_1_2_cout), .B(B2), .SUM(S2), .Cout(fa_1_3_cout));
  FA_1 fa_1_4 (.A(A3), .Cin(fa_1_3_cout), .B(B3), .SUM(S3), .Cout(COUT));

  // Notes on the sheet:
  //   Full Adder
endmodule

// B
module INC_4 (
  input  CIN,
  input  A0,
  input  A1,
  input  A2,
  input  A3,
  output COUT,
  output S0,
  output S1,
  output S2,
  output S3
);

  wire ha_1_1_cout__ab, ha_1_2_cout__ab, ha_1_3_cout__ab;

  HA_1 ha_1_1 (.A(CIN), .B(A0), .COUT__AB(ha_1_1_cout__ab), .SUM__AB_prime__A_prime_B(S0));
  HA_1 ha_1_2 (.A(ha_1_1_cout__ab), .B(A1), .COUT__AB(ha_1_2_cout__ab), .SUM__AB_prime__A_prime_B(S1));
  HA_1 ha_1_3 (.A(ha_1_2_cout__ab), .B(A2), .COUT__AB(ha_1_3_cout__ab), .SUM__AB_prime__A_prime_B(S2));
  HA_1 ha_1_4 (.A(ha_1_3_cout__ab), .B(A3), .COUT__AB(COUT), .SUM__AB_prime__A_prime_B(S3));

  // Notes on the sheet:
  //   4-Bit Increment Schematic
endmodule

module Negate (
  input  PASS_prime_2_sCOMP,
  input  in_2,
  input  in_3,
  input  in_4,
  input  in_5,
  output out_6,
  output out_7,
  output out_8,
  output out_9,
  output out_10
);

  wire xor_1_out, xor_2_out, xor_3_out, xor_4_out;

  xor xor_1 (xor_1_out, PASS_prime_2_sCOMP, in_2);
  xor xor_2 (xor_2_out, PASS_prime_2_sCOMP, in_3);
  xor xor_3 (xor_3_out, PASS_prime_2_sCOMP, in_4);
  xor xor_4 (xor_4_out, PASS_prime_2_sCOMP, in_5);
  INC_4 inc_4_1 (
    .CIN(PASS_prime_2_sCOMP), .A0(xor_4_out), .A1(xor_3_out), .A2(xor_2_out), .A3(xor_1_out), .COUT(out_6),
    .S0(out_7), .S1(out_8), .S2(out_9), .S3(out_10));
endmodule

module MUX_1 (
  input  A,
  input  A_B_prime,
  input  B,
  output Y
);

  wire and_1_out, and_2_out, not_1_out;

  not not_1 (not_1_out, A_B_prime);
  and and_1 (and_1_out, A, not_1_out);
  and and_2 (and_2_out, A_B_prime, B);
  or or_1 (Y, and_1_out, and_2_out);
endmodule

module MUX_4 (
  input  S,
  input  A3,
  input  B3,
  input  A2,
  input  B2,
  input  A1,
  input  B1,
  input  A0,
  input  B0,
  output Y3,
  output Y2,
  output Y1,
  output Y0
);

  MUX_1 mux_1_1 (.A(A3), .A_B_prime(S), .B(B3), .Y(Y3));
  MUX_1 mux_1_2 (.A(A2), .A_B_prime(S), .B(B2), .Y(Y2));
  MUX_1 mux_1_3 (.A(A1), .A_B_prime(S), .B(B1), .Y(Y1));
  MUX_1 mux_1_4 (.A(A0), .A_B_prime(S), .B(B0), .Y(Y0));

  // Notes on the sheet:
  //   MUX_4 A/B' = 0, A = 12, B = 7
endmodule

module DEMUX_1 (
  input  I,
  input  S,
  output A,
  output B
);

  and and_1 (A, I, S);
  and and_2 (B, I, ~S);  // AND_Gate

  // Notes on the sheet:
  //   1-Bit Demultiplexer SOP Form
  //   I = IN
  //   S = Switch (A/B')
endmodule

module DEMUX_4 (
  input  D3,
  input  D2,
  input  D1,
  input  D0,
  input  A_B,
  output A3,
  output B3,
  output A2,
  output B2,
  output A1,
  output B1,
  output A0,
  output B0
);

  DEMUX_1 demux_1_1 (.S(A_B), .B(B3), .I(D3), .A(A3));
  DEMUX_1 demux_1_2 (.S(A_B), .B(B2), .I(D2), .A(A2));
  DEMUX_1 demux_1_3 (.S(A_B), .B(B1), .I(D1), .A(A1));
  DEMUX_1 demux_1_4 (.S(A_B), .B(B0), .I(D0), .A(A0));
endmodule

module Add_Subt (
  input  Switch,
  input  B3,
  input  B2,
  input  B1,
  input  B0,
  input  A3,
  input  A2,
  input  A1,
  input  A0,
  output out_10
);

  wire inc_4_1_s0, inc_4_1_s1, inc_4_1_s2, inc_4_1_s3, xor_1_out, xor_2_out, xor_3_out, xor_4_out;
  wire [3:0] fa_4_1_s0;

  xor xor_1 (xor_1_out, Switch, B3);
  xor xor_2 (xor_2_out, Switch, B2);
  xor xor_3 (xor_3_out, Switch, B1);
  xor xor_4 (xor_4_out, Switch, B0);
  INC_4 inc_4_1 (
    .CIN(Switch), .A0(xor_4_out), .A1(xor_3_out), .A2(xor_2_out), .A3(xor_1_out), .S0(inc_4_1_s0),
    .S1(inc_4_1_s1), .S2(inc_4_1_s2), .S3(inc_4_1_s3));  // open: COUT
  FA_4 fa_4_1 (
    .CIN(1'b0), .A0(inc_4_1_s0), .A1(inc_4_1_s1), .B0(A0), .B1(A1), .A2(inc_4_1_s2), .B2(A2),
    .A3(inc_4_1_s3), .B3(A3), .S0(fa_4_1_s0[0]), .S1(fa_4_1_s0[1]), .S2(fa_4_1_s0[2]), .S3(fa_4_1_s0[3]),
    .COUT(out_10));
  Hex_Digit_Display hex_digit_display_1 (.value(fa_4_1_s0));  // open: dp

  // Notes on the sheet:
  //   +|- : 0|1
  //   Format goes X = A + B or A - B, order matters!
endmodule

module test (
  input  A_B_prime,
  input  A_B_prime_2,
  input  A_B_prime_3,
  input  A_B_prime_4,
  input  A_B_prime_5
);

  INC_4 inc_4_1 (
    .CIN(A_B_prime), .A0(A_B_prime_5), .A1(A_B_prime_4), .A2(A_B_prime_3), .A3(A_B_prime_2));  // open: COUT, S0, S1, S2, S3
endmodule
